# Fritzing sketch booster (saved by Fritzing 0.9.2b)
breadboards: 1

parts:
  Q1 = NPN-Transistor [package="TO92 [THT]"]
  L1 = Inductor [inductance=2.2mH package="400 mil [THT]"]
  Q2 = NPN-Transistor [package="TO92 [THT]"]
  R4 = Resistor [tolerance=±5% resistance=1k package=THT]
  R2 = Resistor [tolerance=±5% resistance=10k package=THT]
  R5 = Resistor [tolerance=±5% resistance=10k package=THT]
  Q3 = Basic FET N-Channel [part_number=IRF710 package="TO220 [THT]"]
  R3 = Resistor [tolerance=±5% resistance=100 package=THT]
  R6 = Resistor [tolerance=±5% resistance=100 package=THT]
  Q4 = Basic FET N-Channel [part_number=IRF710 package="TO220 [THT]"]
  VCC1 = Battery block 9V [part_number=7.4V]
  Arduino_Uno = Arduino Uno (Rev3)
  L2 = Inductor [package="400 mil [THT]"]
  D2 = Rectifier Diode [part_number=1N4007 package="Melf DO-213 AB [SMD]"]
  D1 = Rectifier Diode [part_number=1N4007 package="300 mil [THT]"]
  R1 = Resistor [tolerance=±5% resistance=1k package=THT]
  C1 = Electrolytic Capacitor [capacitance=47µF package="300 mil [THT, electrolytic]"]

nets:
  N1: Q1.E, R2.Pin_1, R3.Pin_0
  N2: Q1.B, R1.Pin_1
  N3: Q1.C, L1.pin_0, Q2.C, VCC1.+, Arduino_Uno.VIN
  N4: L1.pin_1, Q3.drain, D1.anode
  N5: Q2.E, R5.Pin_1, R6.Pin_0
  N6: Q2.B, R4.Pin_1
  N7: R4.Pin_0, Arduino_Uno.D9_PWM
  N8: R2.Pin_0, R5.Pin_0, Q3.source, Q4.source, VCC1.-, Arduino_Uno.GND, C1.-
  N9: Q3.gate, R3.Pin_1
  N10: R6.Pin_1, Q4.gate
  N11: Q4.drain, L2.pin_1, D2.anode
  N12: Arduino_Uno.D8, R1.Pin_0
  N13: L2.pin_0, D2.cathode, D1.cathode, C1.+
